# Fritzing sketch wiring (saved by Fritzing 0.9.3b)
circuit board: 10.1322cm x 5.74437cm
breadboards: 1

parts:
  U1 = 7-SEGMENT-DISPLAY [package=7-segment-display]
  Bauteil1 = Arduino Nano (Rev3.0)
  R2 = Resistor [tolerance=±5% resistance=330 package="1206 [SMD]"]
  R3 = Resistor [tolerance=±5% resistance=330 package="1206 [SMD]"]
  S1 = Taiway 100-SP-X-T1 SPDT Miniature Toggle Switch [part_number=100-SP-X-T1-0-0-B1-M1 package=THT]
  VCC1 = Battery block 9V
  R4 = Rotary Potentiometer (Large) [maximum_resistance=100kΩ package=THT]
  Part1 = KY-006 Passive Buzzer Module [package="Breakout board"]
  TTP223B2 = TTP223B Capacitive Touch Sensor Module

nets:
  N1: U1.E, Bauteil1.D2
  N2: U1.D, Bauteil1.D4
  N3: U1.G1, Bauteil1.D9
  N4: U1.C, Bauteil1.D6
  N5: U1.DP, Bauteil1.D5
  N6: U1.B, Bauteil1.D8
  N7: U1.A, Bauteil1.D7
  N8: U1.G2, U1.F, R2.Pin_0, R3.Pin_0
  N9: U1.G, Bauteil1.D3
  GND: Bauteil1.GND, VCC1.-, R4.leg1, Part1.-, TTP223B2.GND
  N10: Bauteil1.D10, R2.Pin_1
  N11: Bauteil1.D11/MOSI, R3.Pin_1
  N12: Bauteil1.VIN, S1.COM
  N13: Bauteil1.A0, R4.wiper
  N14: Bauteil1.D13/SCK, TTP223B2.SIG
  N15: S1.L1, VCC1.+
  N16: R4.leg2, Part1.S, TTP223B2.VCC

custom parts:
  KY-006 Passive Buzzer Module: Passive Piezoelectric Buzzer Module Keyes KY-006, it can produce a range of sound tones depending on the input frequency.
  TTP223B Capacitive Touch Sensor Module: The TTP223B capacitive touch sensor module uses the TTP223B IC. The appropriate voltage is approximately 2 to 5.5 volts.
